// Logisim project cpu.circ as structural Verilog: 14 circuits, main circuit main
module main (
  input  reset,
  output [31:0] out_2,
  output out_3,
  output [4:0] out_4,
  output [31:0] out_5,
  output out_6,
  output [4:0] out_7,
  output [31:0] out_8
);

  wire ALUSrc, clk, Extop, lui, Zero;
  wire [1:0] MemtoReg, NPCop, RegDst;
  wire [2:0] ALUcontrol;
  wire [4:0] \指令寄存器__15_11 , \指令寄存器__20_16 , \指令寄存器__25_21 ;
  wire [5:0] \指令寄存器_func , \指令寄存器_op ;
  wire [15:0] \指令寄存器_imm15 ;
  wire [25:0] \指令寄存器_imm26 ;
  wire [31:0] ALU_result, EXT_out_3, IFU_tonpc, multiplexer_3_out, multiplexer_4_out, npc_1_npc, pc_4, ra,
       sel_lui, \数据存储器_1_rd ;

  Clock u_clk (.out(clk));
  // Probe on npc_1_npc
  // Probe on out_2
  IFU IFU (.NPC(npc_1_npc), .clk(clk), .reset(reset), .Instr(out_2), .toNPC(IFU_tonpc));
  NPC npc_1 (.pc(IFU_tonpc), .Imm26(\指令寄存器_imm26 ), .Zero(Zero), .NPCop(NPCop), .ra(ra), .pc_4(pc_4), .npc(npc_1_npc));
  \指令存储器  \u_指令寄存器  (
    .Instr(out_2), .op(\指令寄存器_op ), .func(\指令寄存器_func ), ._20_16(\指令寄存器__20_16 ), ._25_21(\指令寄存器__25_21 ),
    ._15_11(\指令寄存器__15_11 ), .Imm15(\指令寄存器_imm15 ), .Imm26(\指令寄存器_imm26 ));
  EXT EXT (.in_1(\指令寄存器_imm15 ), .Extop(Extop), .out_3(EXT_out_3));
  // Probe on out_5
  \控制单元  \u_控制单元_1  (
    .op(\指令寄存器_op ), .MemtoReg(MemtoReg), .MemWrite(out_6), .Branch(NPCop), .ALUop(ALUcontrol),
    .ALUSrc(ALUSrc), .RegDst(RegDst), .RegWrite(out_3), .Extop(Extop), .lui(lui), .func(\指令寄存器_func ));
  Multiplexer #(.select(2), .width(5)) multiplexer_1 (
    .in0(\指令寄存器__20_16 ), .in1(\指令寄存器__15_11 ), .in2({5{1'b1}}), .out(out_4), .sel(RegDst));  // open: in3, en
  \寄存器文件  \u_寄存器文件  (
    .A1(\指令寄存器__25_21 ), .A2(\指令寄存器__20_16 ), .A3(out_4), .WD3(out_5), .RD1(ra), .RD2(out_8), .clk(clk),
    .reset(reset), .WE3(out_3));
  Multiplexer #(.select(2), .width(32)) multiplexer_2 (
    .in0(multiplexer_4_out), .in1(\数据存储器_1_rd ), .in2(pc_4), .out(out_5), .sel(MemtoReg));  // open: in3, en
  shift16 shift16 (.in_1(EXT_out_3), .out_2(sel_lui));
  Multiplexer #(.width(32)) multiplexer_3 (
    .in0(out_8), .in1(EXT_out_3), .out(multiplexer_3_out), .sel(ALUSrc));  // open: en
  ALU ALU (.srcA(ra), .srcB(multiplexer_3_out), .result(ALU_result), .ALUop(ALUcontrol), .Zero(Zero));
  _32to5 u_32to5_1 (.in_1(ALU_result), .out_2(out_7));
  Multiplexer #(.width(32)) multiplexer_4 (
    .in0(ALU_result), .in1(sel_lui), .out(multiplexer_4_out), .sel(lui));  // open: en
  \数据存储器  \u_数据存储器_1  (.MemAddr(out_7), .MemData(out_8), .clk(clk), .reset(reset), .RD(\数据存储器_1_rd ), .MemWrite(out_6));

  // Other names for the same wires on the sheet: Instr[31:0] = out_2; MemAddr[4:0] = out_7; MemData[31:0] = out_8;
  //   MemWrite = out_6; RegAddr[4:0] = out_4; RegData[31:0] = out_5; RegWrite = out_3
endmodule

module \寄存器文件  (
  input  clk,
  input  reset,
  input  WE3,
  input  [4:0] A1,
  input  [4:0] A2,
  input  [4:0] A3,
  input  [31:0] WD3,
  output [31:0] RD1,
  output [31:0] RD2
);

  wire [31:0] I0, I1, I2, I3, I4, I5, I6, I7, I8, I9, I10, I11, I12, I13, I14, I15, I16, I17, I18, I19, I20,
       I21, I22, I23, I24, I25, I26, I27, I28, I29, I30, I31, O0, O1, O2, O3, O4, O5, O6, O7, O8, O9, O10,
       O11, O12, O13, O14, O15, O16, O17, O18, O19, O20, O21, O22, O23, O24, O25, O26, O27, O28, O29, O30,
       O31;

  Demultiplexer #(.select(5), .width(32), .tristate("true")) demultiplexer_1 (
    .out0(I0), .out1(I1), .out2(I2), .out3(I3), .out4(I4), .out5(I5), .out6(I6), .out7(I7), .out8(I8),
    .out9(I9), .out10(I10), .out11(I11), .out12(I12), .out13(I13), .out14(I14), .out15(I15), .out16(I16),
    .out17(I17), .out18(I18), .out19(I19), .out20(I20), .out21(I21), .out22(I22), .out23(I23), .out24(I24),
    .out25(I25), .out26(I26), .out27(I27), .out28(I28), .out29(I29), .out30(I30), .out31(I31), .in(WD3),
    .sel(A3), .en(WE3));
  Register #(.width(32)) register_1 (.D(I0), .en(WE3), .Q(O0), .clk(clk), .clr(1'b1));
  Register #(.width(32)) register_2 (.D(I8), .en(WE3), .Q(O8), .clk(clk), .clr(reset));
  Register #(.width(32)) register_3 (.D(I16), .en(WE3), .Q(O16), .clk(clk), .clr(reset));
  Register #(.width(32)) register_4 (.D(I24), .en(WE3), .Q(O24), .clk(clk), .clr(reset));
  Register #(.width(32)) register_5 (.D(I1), .en(WE3), .Q(O1), .clk(clk), .clr(reset));
  Register #(.width(32)) register_6 (.D(I9), .en(WE3), .Q(O9), .clk(clk), .clr(reset));
  Register #(.width(32)) register_7 (.D(I17), .en(WE3), .Q(O17), .clk(clk), .clr(reset));
  Register #(.width(32)) register_8 (.D(I25), .en(WE3), .Q(O25), .clk(clk), .clr(reset));
  Register #(.width(32)) register_9 (.D(I2), .en(WE3), .Q(O2), .clk(clk), .clr(reset));
  Register #(.width(32)) register_10 (.D(I10), .en(WE3), .Q(O10), .clk(clk), .clr(reset));
  Register #(.width(32)) register_11 (.D(I18), .en(WE3), .Q(O18), .clk(clk), .clr(reset));
  Register #(.width(32)) register_12 (.D(I26), .en(WE3), .Q(O26), .clk(clk), .clr(reset));
  Register #(.width(32)) register_13 (.D(I3), .en(WE3), .Q(O3), .clk(clk), .clr(reset));
  Register #(.width(32)) register_14 (.D(I11), .en(WE3), .Q(O11), .clk(clk), .clr(reset));
  Register #(.width(32)) register_15 (.D(I19), .en(WE3), .Q(O19), .clk(clk), .clr(reset));
  Register #(.width(32)) register_16 (.D(I27), .en(WE3), .Q(O27), .clk(clk), .clr(reset));
  Register #(.width(32)) register_17 (.D(I4), .en(WE3), .Q(O4), .clk(clk), .clr(reset));
  Register #(.width(32)) register_18 (.D(I12), .en(WE3), .Q(O12), .clk(clk), .clr(reset));
  Register #(.width(32)) register_19 (.D(I20), .en(WE3), .Q(O20), .clk(clk), .clr(reset));
  Register #(.width(32)) register_20 (.D(I28), .en(WE3), .Q(O28), .clk(clk), .clr(reset));
  Multiplexer #(.select(5), .width(32)) multiplexer_1 (
    .in0(O0), .in1(O1), .in2(O2), .in3(O3), .in4(O4), .in5(O5), .in6(O6), .in7(O7), .in8(O8), .in9(O9),
    .in10(O10), .in11(O11), .in12(O12), .in13(O13), .in14(O14), .in15(O15), .in16(O16), .in17(O17),
    .in18(O18), .in19(O19), .in20(O20), .in21(O21), .in22(O22), .in23(O23), .in24(O24), .in25(O25),
    .in26(O26), .in27(O27), .in28(O28), .in29(O29), .in30(O30), .in31(O31), .out(RD1), .sel(A1));  // open: en
  Register #(.width(32)) register_21 (.D(I5), .en(WE3), .Q(O5), .clk(clk), .clr(reset));
  Register #(.width(32)) register_22 (.D(I13), .en(WE3), .Q(O13), .clk(clk), .clr(reset));
  Register #(.width(32)) register_23 (.D(I21), .en(WE3), .Q(O21), .clk(clk), .clr(reset));
  Register #(.width(32)) register_24 (.D(I29), .en(WE3), .Q(O29), .clk(clk), .clr(reset));
  Register #(.width(32)) register_25 (.D(I6), .en(WE3), .Q(O6), .clk(clk), .clr(reset));
  Register #(.width(32)) register_26 (.D(I14), .en(WE3), .Q(O14), .clk(clk), .clr(reset));
  Register #(.width(32)) register_27 (.D(I22), .en(WE3), .Q(O22), .clk(clk), .clr(reset));
  Register #(.width(32)) register_28 (.D(I30), .en(WE3), .Q(O30), .clk(clk), .clr(reset));
  Register #(.width(32)) register_29 (.D(I7), .en(WE3), .Q(O7), .clk(clk), .clr(reset));
  Register #(.width(32)) register_30 (.D(I15), .en(WE3), .Q(O15), .clk(clk), .clr(reset));
  Register #(.width(32)) register_31 (.D(I23), .en(WE3), .Q(O23), .clk(clk), .clr(reset));
  Register #(.width(32)) register_32 (.D(I31), .en(WE3), .Q(O31), .clk(clk), .clr(reset));
  Multiplexer #(.select(5), .width(32)) multiplexer_2 (
    .in0(O0), .in1(O1), .in2(O2), .in3(O3), .in4(O4), .in5(O5), .in6(O6), .in7(O7), .in8(O8), .in9(O9),
    .in10(O10), .in11(O11), .in12(O12), .in13(O13), .in14(O14), .in15(O15), .in16(O16), .in17(O17),
    .in18(O18), .in19(O19), .in20(O20), .in21(O21), .in22(O22), .in23(O23), .in24(O24), .in25(O25),
    .in26(O26), .in27(O27), .in28(O28), .in29(O29), .in30(O30), .in31(O31), .out(RD2), .sel(A2));  // open: en
endmodule

module \指令存储器  (
  input  [31:0] Instr,
  output [5:0] op,
  output [5:0] func,
  output [4:0] _25_21,
  output [4:0] _20_16,
  output [4:0] _15_11,
  output [15:0] Imm15,
  output [25:0] Imm26
);


  assign _15_11 = Instr[15:11];
  assign _20_16 = Instr[20:16];
  assign _25_21 = Instr[25:21];
  assign func = Instr[5:0];
  assign Imm15 = Instr[15:0];
  assign Imm26 = Instr[25:0];
  assign op = Instr[31:26];
endmodule

module IFU (
  input  [31:0] NPC,
  input  clk,
  input  reset,
  output [31:0] Instr,
  output [31:0] toNPC
);

  Register #(.width(32)) PC (.D(NPC), .Q(toNPC), .clk(clk), .clr(reset));  // open: en
  ROM #(.addrWidth(5), .dataWidth(32)) rom_1 (.addr(toNPC[6:2]), .data(Instr));  // open: sel

  // Notes on the sheet:
  //   contents of rom_1 (hex, n*v repeats v):
  //   34080001 c000c03 10000003 35080002 1084821 3e00008 1002021
endmodule

module ALU (
  input  [2:0] ALUop,
  input  [31:0] srcA,
  input  [31:0] srcB,
  output Zero,
  output [31:0] result
);

  wire [31:0] adder_1_out, or_1_out, subtractor_1_out;

  Adder #(.width(32)) adder_1 (.a(srcA), .b(srcB), .out(adder_1_out));  // open: cin, cout
  Subtractor #(.width(32)) subtractor_1 (.a(srcA), .b(srcB), .out(subtractor_1_out));  // open: bin, bout
  assign or_1_out = srcA | srcB;  // OR_Gate or_1, 32 bits wide
  Comparator #(.width(32), .mode("unsigned")) comparator_1 (.a(srcA), .b(srcB), .eq(Zero));  // open: gt, lt
  Multiplexer #(.select(3), .width(32)) multiplexer_1 (
    .in0(adder_1_out), .in1(subtractor_1_out), .in2(or_1_out), .out(result), .sel(ALUop));  // open: in3, in4, in5, in6, in7, en

  // Other names for the same wires on the sheet: src1[31:0] = srcA; src2[31:0] = srcB
endmodule

module \数据存储器  (
  input  [4:0] MemAddr,
  input  [31:0] MemData,
  input  clk,
  input  reset,
  input  MemWrite,
  output [31:0] RD
);

  RAM #(.addrWidth(5), .dataWidth(32), .bus("separate")) ram_1 (
    .addr(MemAddr), .din(MemData), .data(RD), .str(MemWrite), .clk(clk), .clr(reset));  // open: sel, ld
endmodule

module _32to5 (
  input  [31:0] in_1,
  output [4:0] out_2
);


  assign out_2 = in_1[6:2];
endmodule

module \控制单元  (
  input  [5:0] op,
  input  [5:0] func,
  output [1:0] MemtoReg,
  output MemWrite,
  output Extop,
  output [1:0] Branch,
  output [2:0] ALUop,
  output ALUSrc,
  output [1:0] RegDst,
  output RegWrite,
  output lui
);

  wire add_out, addu_out, and_1_out, and_2_out, and_3_out, beq_out, jr_2_out, jr_out, lui_out, lw_out,
       not_1_out, not_2_out, not_3_out, not_4_out, not_5_out, not_6_out, not_7_out, not_8_out, not_9_out,
       not_10_out, not_11_out, not_12_out, ori_out, sub_out, subu_out, sw_out;

  not not_1 (not_1_out, op[0]);
  not not_2 (not_2_out, op[1]);
  not not_3 (not_3_out, op[3]);
  not not_4 (not_4_out, op[2]);
  not not_5 (not_5_out, op[4]);
  not not_6 (not_6_out, op[5]);
  and add (add_out, not_6_out, not_5_out, not_3_out, not_4_out, not_2_out, not_1_out);
  and ori (ori_out, not_6_out, not_5_out, op[3], op[2], not_2_out, op[0]);
  and sub (sub_out, not_6_out, not_5_out, not_3_out, not_4_out, not_2_out, not_1_out);
  and lw (lw_out, op[5], not_5_out, not_3_out, not_4_out, op[1], op[0]);
  and sw (sw_out, op[5], not_5_out, op[3], not_4_out, op[1], op[0]);
  and beq (beq_out, not_6_out, not_5_out, not_3_out, op[2], not_2_out, not_1_out);
  and u_lui (lui_out, not_6_out, not_5_out, op[3], op[2], op[1], op[0]);
  and jal (MemtoReg[1], not_6_out, not_5_out, not_3_out, not_4_out, op[1], op[0]);
  and jr (jr_out, not_6_out, not_5_out, not_3_out, not_4_out, not_2_out, not_1_out);
  not not_7 (not_7_out, func[0]);
  not not_8 (not_8_out, func[2]);
  not not_9 (not_9_out, func[1]);
  not not_10 (not_10_out, func[3]);
  not not_11 (not_11_out, func[4]);
  not not_12 (not_12_out, func[5]);
  and and_1 (and_1_out, func[5], not_11_out, not_10_out, not_8_out, not_9_out, func[0]);
  and and_2 (and_2_out, func[5], not_11_out, not_10_out, not_8_out, func[1], func[0]);
  and and_3 (and_3_out, not_12_out, not_11_out, func[3], not_8_out, not_9_out, not_7_out);
  and addu (addu_out, add_out, and_1_out);
  and subu (subu_out, sub_out, and_2_out);
  and jr_2 (jr_2_out, jr_out, and_3_out);
  or u_MemtoReg (MemtoReg[0], beq_out, sw_out, lw_out);
  buf u_MemWrite (MemWrite, sw_out);  // OR_Gate
  or u_Extop (Extop, addu_out, subu_out, lw_out, lw_out, beq_out);
  or u_Branch (Branch[0], jr_2_out, beq_out);
  or Branch1 (Branch[1], MemtoReg[1], jr_2_out);
  or u_ALUSrc (ALUSrc, ori_out, sw_out, lw_out);
  or u_RegDst (RegDst[1], MemtoReg[1], jr_2_out);
  or RegDst1 (RegDst[0], addu_out, subu_out, sw_out, beq_out);
  or u_RegWrite (RegWrite, MemtoReg[1], addu_out, ori_out, subu_out, lw_out, lui_out);
  buf lui_2 (lui, lui_out);  // OR_Gate
  _1 u_1_1 (
    .in0(addu_out), .in1(ori_out), .in2(subu_out), .in3(lw_out), .in4(sw_out), .in5(beq_out), .in6(lui_out),
    .o0(ALUop[2]), .o1(ALUop[1]), .o2(ALUop[0]));

  // Other names for the same wires on the sheet: s0 = func[0]; s1 = func[1]; s2 = func[2]; s3 = func[3]; s4 = func[4];
  //   s5 = func[5]
endmodule

module \ALU译码器  (
  input  [2:0] ALUop,
  input  [5:0] func,
  output [2:0] ALUcontrol
);

  wire not_1_out, not_2_out, not_3_out, not_4_out, not_5_out, not_6_out, not_7_out, not_8_out, not_9_out;
  wire [2:0] addu_out;

  not not_1 (not_1_out, func[0]);
  not not_2 (not_2_out, func[1]);
  not not_3 (not_3_out, func[3]);
  not not_4 (not_4_out, func[2]);
  not not_5 (not_5_out, func[4]);
  not not_6 (not_6_out, func[5]);
  not not_7 (not_7_out, ALUop[0]);
  not not_8 (not_8_out, ALUop[1]);
  not not_9 (not_9_out, ALUop[2]);
  and addu (addu_out[0], not_9_out, not_8_out, not_7_out, func[5], not_5_out, not_3_out, not_4_out, not_2_out, func[0]);
  and subu (addu_out[1], not_9_out, not_8_out, not_7_out, func[5], not_5_out, not_3_out, not_4_out, func[1], func[0]);
  and jr (addu_out[2], not_9_out, not_8_out, not_7_out, not_6_out, not_5_out, not_3_out, func[2], not_2_out, func[0]);
  Multiplexer #(.select(3), .width(3)) multiplexer_1 (
    .in0(ALUop), .in2(3'b001), .in4(3'b001), .out(ALUcontrol), .sel(addu_out));  // open: in1, in3, in5, in6, in7, en

  // Other names for the same wires on the sheet: s0 = ALUop[0]; s1 = ALUop[1]; s2 = ALUop[2]; op0 = func[0];
  //   op1 = func[1]; op2 = func[2]; op3 = func[3]; op4 = func[4]; op5 = func[5]
endmodule

module EXT (
  input  [15:0] in_1,
  input  Extop,
  output [31:0] out_3
);

  wire [31:0] bit_extender_1_out, bit_extender_2_out;

  assign bit_extender_1_out = {{16{1'b0}}, in_1};  // Bit_Extender bit_extender_1
  assign bit_extender_2_out = {{16{in_1[15]}}, in_1};  // Bit_Extender bit_extender_2
  Multiplexer #(.width(32)) multiplexer_1 (
    .in0(bit_extender_1_out), .in1(bit_extender_2_out), .out(out_3), .sel(Extop));  // open: en
endmodule

module shift2 (
  input  [31:0] in_1,
  output [31:0] out_2
);

  Shifter #(.width(32)) shifter_1 (.in(in_1), .\dist (5'b00010), .out(out_2));
endmodule

module shift16 (
  input  [31:0] in_1,
  output [31:0] out_2
);

  Shifter #(.width(32)) shifter_1 (.in(in_1), .\dist (5'b10000), .out(out_2));
endmodule

module _1 (
  input  in0,
  input  in1,
  input  in2,
  input  in3,
  input  in4,
  input  in5,
  input  in6,
  output o0,
  output o1,
  output o2
);

  wire and_1_out, and_2_out, and_3_out, and_4_out, and_5_out, and_6_out, and_7_out, and_8_out, and_9_out,
       and_10_out, and_11_out, and_12_out, and_13_out, and_14_out, and_15_out, and_16_out, and_17_out,
       and_18_out, and_19_out, and_20_out, not_1_out, not_2_out, not_3_out, not_4_out, not_5_out, not_6_out,
       not_7_out, not_8_out, not_9_out, not_10_out, not_11_out, not_12_out, not_13_out, not_14_out,
       not_15_out, not_16_out, not_17_out, not_18_out, not_19_out, not_20_out, not_21_out, not_22_out,
       not_23_out, not_24_out, not_25_out, not_26_out, not_27_out, not_28_out, not_29_out, not_30_out;

  not not_1 (not_1_out, in0);
  not not_2 (not_2_out, in1);
  not not_3 (not_3_out, in2);
  not not_4 (not_4_out, in3);
  not not_5 (not_5_out, in4);
  not not_6 (not_6_out, in5);
  not not_7 (not_7_out, in0);
  not not_8 (not_8_out, in1);
  not not_9 (not_9_out, in2);
  not not_10 (not_10_out, in3);
  not not_11 (not_11_out, in4);
  not not_12 (not_12_out, in6);
  not not_13 (not_13_out, in0);
  not not_14 (not_14_out, in2);
  not not_15 (not_15_out, in3);
  not not_16 (not_16_out, in4);
  not not_17 (not_17_out, in5);
  not not_18 (not_18_out, in6);
  not not_19 (not_19_out, in0);
  not not_20 (not_20_out, in1);
  not not_21 (not_21_out, in2);
  not not_22 (not_22_out, in3);
  not not_23 (not_23_out, in4);
  not not_24 (not_24_out, in6);
  not not_25 (not_25_out, in0);
  not not_26 (not_26_out, in1);
  not not_27 (not_27_out, in3);
  not not_28 (not_28_out, in4);
  not not_29 (not_29_out, in5);
  not not_30 (not_30_out, in6);
  and and_1 (and_1_out, not_1_out, not_2_out, not_3_out, not_4_out, not_5_out, not_6_out);
  and and_2 (and_2_out, in4, in5);
  and and_3 (and_3_out, in3, in5);
  and and_4 (and_4_out, in3, in4);
  and and_5 (and_5_out, in2, in5);
  and and_6 (and_6_out, in2, in4);
  and and_7 (and_7_out, in2, in3);
  and and_8 (and_8_out, in1, in5);
  and and_9 (and_9_out, in1, in4);
  and and_10 (and_10_out, in1, in3);
  and and_11 (and_11_out, in1, in2);
  and and_12 (and_12_out, in0, in5);
  and and_13 (and_13_out, in0, in4);
  and and_14 (and_14_out, in0, in3);
  and and_15 (and_15_out, in0, in2);
  and and_16 (and_16_out, in0, in1);
  and and_17 (and_17_out, not_7_out, not_8_out, not_9_out, not_10_out, not_11_out, in5, not_12_out);
  and and_18 (and_18_out, not_13_out, in1, not_14_out, not_15_out, not_16_out, not_17_out, not_18_out);
  and and_19 (and_19_out, not_19_out, not_20_out, not_21_out, not_22_out, not_23_out, in5, not_24_out);
  and and_20 (and_20_out, not_25_out, not_26_out, in2, not_27_out, not_28_out, not_29_out, not_30_out);
  or or_1 (o1, and_17_out, and_18_out);
  or or_2 (o2, and_19_out, and_20_out);
  or or_3 (o0, and_1_out, in6, and_2_out, and_3_out, and_4_out, and_5_out, and_6_out, and_7_out, and_8_out, and_9_out, and_10_out, and_11_out, and_12_out, and_13_out, and_14_out, and_15_out, and_16_out);
endmodule

module NPC (
  input  [31:0] pc,
  input  [25:0] Imm26,
  input  Zero,
  input  [1:0] NPCop,
  input  [31:0] ra,
  output [31:0] pc_4,
  output [31:0] npc
);

  wire [31:0] adder_1_out, bit_extender_1_out, multiplexer_1_out;

  assign bit_extender_1_out = {{14{Imm26[15]}}, {Imm26[15:0], 2'b00}};  // Bit_Extender bit_extender_1
  Multiplexer #(.width(32)) multiplexer_1 (
    .in0(pc_4), .in1(adder_1_out), .out(multiplexer_1_out), .sel(Zero));  // open: en
  Adder #(.width(32)) adder_1 (.a(pc_4), .b(bit_extender_1_out), .out(adder_1_out));  // open: cin, cout
  Adder #(.width(32)) adder_2 (.a(pc), .b(32'h4), .out(pc_4));  // open: cin, cout
  Multiplexer #(.select(2), .width(32)) multiplexer_2 (
    .in0(pc_4), .in1(multiplexer_1_out), .in2({pc[31:28], Imm26, 2'b00}), .in3(ra), .out(npc), .sel(NPCop));  // open: en
endmodule
