// Logisim project CRC.circ as structural Verilog: 2 circuits, main circuit CRC
module CRC (
  input  [7:0] A,
  input  [3:0] B,
  output [10:0] C
);

  wire [3:1] div_2_out_3, div_3_out_3, div_4_out_3, div_5_out_3, div_6_out_3, div_7_out_3, div_8_out_3;
  wire [10:0] bit_extender_1_out, shifter_1_out;

  assign bit_extender_1_out = {{3{1'b0}}, A};  // Bit_Extender bit_extender_1
  Shifter #(.width(11)) shifter_1 (.in(bit_extender_1_out), .\dist (4'b0011), .out(shifter_1_out));
  div div_1 (.in_1({div_2_out_3, shifter_1_out[0]}), .in_2(B), .out_3(C[2:0]));
  div div_2 (.in_1({div_3_out_3, shifter_1_out[1]}), .in_2(B), .out_3(div_2_out_3));
  div div_3 (.in_1({div_4_out_3, shifter_1_out[2]}), .in_2(B), .out_3(div_3_out_3));
  div div_4 (.in_1({div_5_out_3, shifter_1_out[3]}), .in_2(B), .out_3(div_4_out_3));
  div div_5 (.in_1({div_6_out_3, shifter_1_out[4]}), .in_2(B), .out_3(div_5_out_3));
  div div_6 (.in_1({div_8_out_3, shifter_1_out[5]}), .in_2(B), .out_3(div_6_out_3));
  div div_7 (.in_1(shifter_1_out[10:7]), .in_2(B), .out_3(div_7_out_3));
  div div_8 (.in_1({div_7_out_3, shifter_1_out[6]}), .in_2(B), .out_3(div_8_out_3));

  assign C[10:3] = A;

  // Other names for the same wires on the sheet: check[2:0] = C[2:0]; CRC[7:0] = A; divisor[3:0] = B
endmodule

module div (
  input  [3:0] in_1,
  input  [3:0] in_2,
  output [2:0] out_3
);

  wire select;
  wire [3:0] multiplexer_1_out, xor_1_out;

  Comparator #(.width(1), .mode("unsigned")) comparator_1 (.a(1'b1), .b(in_1[3]), .eq(select));  // open: gt, lt
  assign xor_1_out = in_1 ^ in_2;  // XOR_Gate xor_1, 4 bits wide
  Multiplexer #(.width(4)) multiplexer_1 (
    .in0(in_1), .in1(xor_1_out), .out(multiplexer_1_out), .sel(select));  // open: en
  Bit_Extender #(.in_width(4), .out_width(3)) bit_extender_1 (.in(multiplexer_1_out), .out(out_3));
endmodule
