// Logisim project FSM.circ as structural Verilog: 2 circuits, main circuit fsm
module fsm (
  input  CLR,
  input  [1:0] In,
  output Z
);

  wire CLK_out;
  wire [1:0] \状态转移_2_out_3 ;
  wire [2:0] multiplexer_1_out, register_1_q, \状态转移_1_out_3 ;

  Clock CLK (.out(CLK_out));
  \状态转移  \u_状态转移_1  (.status(register_1_q), .In(In), .out_3(\状态转移_1_out_3 ));
  Multiplexer #(.width(3)) multiplexer_1 (
    .in0(\状态转移_1_out_3 ), .in1(3'b000), .out(multiplexer_1_out), .sel(CLR));  // open: en
  Register #(.width(3)) register_1 (.D(multiplexer_1_out), .Q(register_1_q), .clk(CLK_out));  // open: en, clr
  \状态转移  \u_状态转移_2  (.status(register_1_q), .In(In), .out_3({Z, \状态转移_2_out_3 }));
endmodule

module \状态转移  (
  input  [2:0] status,
  input  [1:0] In,
  output [2:0] out_3
);

  wire and_1_out, and_2_out, and_3_out, and_4_out, and_5_out, and_6_out, and_7_out, and_8_out, and_9_out,
       not_1_out, not_2_out, not_3_out, not_4_out, not_5_out, not_6_out, not_7_out, not_8_out, not_9_out,
       not_10_out, not_11_out, not_12_out, not_13_out, not_14_out;

  not not_1 (not_1_out, In[0]);
  not not_2 (not_2_out, status[1]);
  not not_3 (not_3_out, In[1]);
  not not_4 (not_4_out, status[1]);
  not not_5 (not_5_out, In[0]);
  not not_6 (not_6_out, status[0]);
  not not_7 (not_7_out, In[0]);
  not not_8 (not_8_out, status[0]);
  not not_9 (not_9_out, In[1]);
  not not_10 (not_10_out, status[1]);
  not not_11 (not_11_out, In[0]);
  not not_12 (not_12_out, status[0]);
  not not_13 (not_13_out, In[0]);
  not not_14 (not_14_out, In[1]);
  and and_1 (and_1_out, status[1], status[0], not_1_out);
  and and_2 (and_2_out, status[2], status[1]);
  and and_3 (and_3_out, not_2_out, status[0], not_3_out);
  and and_4 (and_4_out, not_4_out, status[0], not_5_out);
  and and_5 (and_5_out, status[1], not_6_out, not_7_out);
  and and_6 (and_6_out, not_8_out, not_9_out, In[0]);
  and and_7 (and_7_out, not_10_out, status[0], not_11_out);
  and and_8 (and_8_out, status[1], not_12_out, not_13_out);
  and and_9 (and_9_out, status[1], not_14_out, In[0]);
  or or_1 (out_3[2], and_1_out, and_2_out);
  or or_2 (out_3[1], and_3_out, and_4_out, and_5_out);
  or or_3 (out_3[0], and_6_out, and_7_out, and_8_out, and_9_out);
endmodule
