// Logisim project Logisim1.circ as structural Verilog
module _2_1mux (
  input  in_00,
  input  in_01,
  input  in_10,
  input  in_11,
  input  sel_0,
  input  sel_1,
  output out
);

  wire n4_1mus_1_out_4, n4_1mus_2_out_4;

  _4_1mus u_4_1mus_1 (.in_0(in_00), .in_1(in_01), .select(sel_1), .out_4(n4_1mus_1_out_4));
  _4_1mus u_4_1mus_2 (.in_0(in_10), .in_1(in_11), .select(sel_1), .out_4(n4_1mus_2_out_4));
  _4_1mus u_4_1mus_3 (.in_0(n4_1mus_1_out_4), .in_1(n4_1mus_2_out_4), .select(sel_0), .out_4(out));
endmodule

module _4_1mus (
  input  in_0,
  input  in_1,
  input  select,
  output out_4
);

  wire and_1_out, and_2_out, not_1_out;

  not not_1 (not_1_out, select);
  and and_1 (and_1_out, in_0, not_1_out);
  and and_2 (and_2_out, in_1, select);
  or or_1 (out_4, and_1_out, and_2_out);
endmodule
