// Logisim project Logisim_Fibonacci.circ as structural Verilog: 3 circuits, main circuit main
module main (
  input  [2:0] in_1,
  output [3:0] out_2
);

  wire \计数模块_1_out_3 ;
  wire [3:0] \计算模块_1_out_3 ;

  \计算模块  \u_计算模块_1  (.freeze(\计数模块_1_out_3 ), .out_3(\计算模块_1_out_3 ));  // open: in_2
  \计数模块  \u_计数模块_1  (.\input (in_1), .out_3(\计数模块_1_out_3 ));  // open: reset
  Multiplexer #(.width(4)) multiplexer_1 (
    .in0(4'b0000), .in1(\计算模块_1_out_3 ), .out(out_2), .sel(\计数模块_1_out_3 ));  // open: en
endmodule

module \计算模块  (
  input  freeze,
  input  in_2,
  output [3:0] out_3
);

  wire clock, enable, initialize;
  wire [3:0] adder_1_out, last, multiplexer_1_out;

  Clock clock_1 (.out(clock));
  not not_1 (enable, freeze);
  Counter #(.width(1), .max('h1), .ongoal("stay")) counter_1 (
    .Q(initialize), .clk(clock), .clr(in_2));  // open: load, D, count, carry
  Multiplexer #(.width(4)) multiplexer_1 (
    .in0(4'b0001), .in1(out_3), .out(multiplexer_1_out), .sel(initialize));  // open: en
  Adder #(.width(4)) adder_1 (.a(out_3), .b(last), .out(adder_1_out));  // open: cin, cout
  Register #(.width(4)) register_1 (.D(multiplexer_1_out), .en(enable), .Q(last), .clk(clock), .clr(in_2));
  Register #(.width(4)) register_2 (.D(adder_1_out), .en(enable), .Q(out_3), .clk(clock), .clr(in_2));

  // Other names for the same wires on the sheet: now[3:0] = out_3; reset = in_2
endmodule

module \计数模块  (
  input  [2:0] \input ,
  input  reset,
  output out_3
);

  wire clock_1_out;
  wire [3:0] bit_extender_1_out, counter_1_q;

  Clock clock_1 (.out(clock_1_out));
  assign bit_extender_1_out = {{1{1'b0}}, \input };  // Bit_Extender bit_extender_1
  Counter #(.width(4), .max('hf), .ongoal("stay")) counter_1 (
    .Q(counter_1_q), .clk(clock_1_out), .clr(reset));  // open: load, D, count, carry
  Comparator #(.width(4), .mode("unsigned")) comparator_1 (
    .a(bit_extender_1_out), .b(counter_1_q), .lt(out_3));  // open: gt, eq
endmodule
