// Logisim project Logisim_Fibonacci2.circ as structural Verilog: 8 circuits, main circuit main
module main (
  input  [31:0] \input ,
  output [31:0] out_2
);

  wire freeze, n_low;

  \计数逻辑  \u_计数逻辑_1  (.\input (\input ), .in_2(1'b0), .n_low(n_low), .freeze(freeze));
  \计算逻辑  \u_计算逻辑_1  (.n_low(n_low), .freeze(freeze), .clr(1'b0), .out_4(out_2));

  // Other names for the same wires on the sheet: output[31:0] = out_2
endmodule

module \矩阵乘法  (
  input  [31:0] A11,
  input  [31:0] A12,
  input  [31:0] A21,
  input  [31:0] A22,
  input  [31:0] B11,
  input  [31:0] B12,
  input  [31:0] B21,
  input  [31:0] B22,
  output [31:0] c11,
  output [31:0] c12,
  output [31:0] c21,
  output [31:0] c22
);

  wire [31:0] multiplier_1_out, multiplier_2_out, multiplier_3_out, multiplier_4_out, multiplier_5_out,
       multiplier_6_out, multiplier_7_out, multiplier_8_out;

  Multiplier #(.width(32)) multiplier_1 (.a(A11), .b(B11), .out(multiplier_1_out));  // open: cin, cout
  Multiplier #(.width(32)) multiplier_2 (.a(A12), .b(B21), .out(multiplier_2_out));  // open: cin, cout
  Multiplier #(.width(32)) multiplier_3 (.a(A11), .b(B12), .out(multiplier_3_out));  // open: cin, cout
  Multiplier #(.width(32)) multiplier_4 (.a(A12), .b(B22), .out(multiplier_4_out));  // open: cin, cout
  Multiplier #(.width(32)) multiplier_5 (.a(A21), .b(B11), .out(multiplier_5_out));  // open: cin, cout
  Multiplier #(.width(32)) multiplier_6 (.a(A22), .b(B21), .out(multiplier_6_out));  // open: cin, cout
  Multiplier #(.width(32)) multiplier_7 (.a(A21), .b(B12), .out(multiplier_7_out));  // open: cin, cout
  Multiplier #(.width(32)) multiplier_8 (.a(A22), .b(B22), .out(multiplier_8_out));  // open: cin, cout
  Adder #(.width(32)) adder_1 (.a(multiplier_1_out), .b(multiplier_2_out), .out(c11));  // open: cin, cout
  Adder #(.width(32)) adder_2 (.a(multiplier_3_out), .b(multiplier_4_out), .out(c12));  // open: cin, cout
  Adder #(.width(32)) adder_3 (.a(multiplier_5_out), .b(multiplier_6_out), .out(c21));  // open: cin, cout
  Adder #(.width(32)) adder_4 (.a(multiplier_7_out), .b(multiplier_8_out), .out(c22));  // open: cin, cout
endmodule

module \矩阵MUX  (
  input  [31:0] A11,
  input  [31:0] A12,
  input  [31:0] A21,
  input  [31:0] A22,
  input  [31:0] B11,
  input  [31:0] B12,
  input  [31:0] B21,
  input  [31:0] B22,
  input  select,
  output [31:0] out11,
  output [31:0] out12,
  output [31:0] out21,
  output [31:0] out22
);

  Multiplexer #(.width(32)) multiplexer_1 (.in0(A11), .in1(B11), .out(out11), .sel(select));  // open: en
  Multiplexer #(.width(32)) multiplexer_2 (.in0(A12), .in1(B12), .out(out12), .sel(select));  // open: en
  Multiplexer #(.width(32)) multiplexer_3 (.in0(A21), .in1(B21), .out(out21), .sel(select));  // open: en
  Multiplexer #(.width(32)) multiplexer_4 (.in0(A22), .in1(B22), .out(out22), .sel(select));  // open: en
endmodule

// 初始值
module \矩阵初始值  (
  output [31:0] out11,
  output [31:0] out12,
  output [31:0] out21,
  output [31:0] out22
);


  assign out11 = 32'h1;
  assign out12 = 32'h1;
  assign out21 = 32'h1;
  assign out22 = {32{1'b0}};
endmodule

module \矩阵寄存器  (
  input  [31:0] A11_in,
  input  [31:0] A12_in,
  input  [31:0] A21_in,
  input  enable,
  input  clock,
  input  clear,
  input  [31:0] A22_in,
  output [31:0] A11_out,
  output [31:0] A12_out,
  output [31:0] A21_out,
  output [31:0] A22_out
);

  Register #(.width(32)) a11 (.D(A11_in), .en(enable), .Q(A11_out), .clk(clock), .clr(clear));
  Register #(.width(32)) a21 (.D(A21_in), .en(enable), .Q(A21_out), .clk(clock), .clr(clear));
  Register #(.width(32)) a12 (.D(A12_in), .en(enable), .Q(A12_out), .clk(clock), .clr(clear));
  Register #(.width(32)) a22 (.D(A22_in), .en(enable), .Q(A22_out), .clk(clock), .clr(clear));
endmodule

module \计算逻辑  (
  input  n_low,
  input  freeze,
  input  clr,
  output [31:0] out_4
);

  wire clk, ena, init;
  wire [31:0] a11, a12, a21, a22, s11, s12, s21, s22, \单位阵_1_out11 , \单位阵_1_out12 , \单位阵_1_out21 ,
       \单位阵_1_out22 , \单位阵_2_out11 , \单位阵_2_out12 , \单位阵_2_out21 , \单位阵_2_out22 , \矩阵mux_1_out11 ,
       \矩阵mux_1_out12 , \矩阵mux_1_out21 , \矩阵mux_1_out22 , \矩阵mux_2_out11 , \矩阵mux_2_out12 , \矩阵mux_2_out21 ,
       \矩阵mux_2_out22 , \矩阵mux_3_out11 , \矩阵mux_3_out12 , \矩阵mux_3_out21 , \矩阵mux_3_out22 , \矩阵乘法_1_c11 ,
       \矩阵乘法_1_c12 , \矩阵乘法_1_c21 , \矩阵乘法_1_c22 , \矩阵乘法_2_c11 , \矩阵乘法_2_c12 , \矩阵乘法_2_c21 , \矩阵乘法_2_c22 ,
       \矩阵初始值_1_out11 , \矩阵初始值_1_out12 , \矩阵初始值_1_out21 , \矩阵初始值_1_out22 ;

  Counter #(.width(1), .max('h1), .ongoal("stay")) counter_1 (
    .Q(init), .clk(clk), .clr(clr));  // open: load, D, count, carry
  Clock u_clk (.out(clk));
  not not_1 (ena, freeze);
  \单位阵  \u_单位阵_1  (.out11(\单位阵_1_out11 ), .out12(\单位阵_1_out12 ), .out21(\单位阵_1_out21 ), .out22(\单位阵_1_out22 ));
  \矩阵MUX  \u_矩阵mux_1  (
    .A11(\单位阵_1_out11 ), .A12(\单位阵_1_out12 ), .A21(\单位阵_1_out21 ), .A22(\单位阵_1_out22 ), .B11(a11), .B12(a12),
    .B21(a21), .B22(a22), .select(n_low), .out11(\矩阵mux_1_out11 ), .out12(\矩阵mux_1_out12 ),
    .out21(\矩阵mux_1_out21 ), .out22(\矩阵mux_1_out22 ));
  \矩阵初始值  \u_矩阵初始值_1  (
    .out11(\矩阵初始值_1_out11 ), .out12(\矩阵初始值_1_out12 ), .out21(\矩阵初始值_1_out21 ), .out22(\矩阵初始值_1_out22 ));
  \矩阵乘法  \u_矩阵乘法_1  (
    .A11(a11), .A12(a12), .A21(a21), .A22(a22), .B11(a11), .B12(a12), .B21(a21), .B22(a22),
    .c11(\矩阵乘法_1_c11 ), .c12(\矩阵乘法_1_c12 ), .c21(\矩阵乘法_1_c21 ), .c22(\矩阵乘法_1_c22 ));
  \矩阵乘法  \u_矩阵乘法_2  (
    .A11(s11), .A12(s12), .A21(s21), .A22(s22), .B11(\矩阵mux_1_out11 ), .B12(\矩阵mux_1_out12 ),
    .B21(\矩阵mux_1_out21 ), .B22(\矩阵mux_1_out22 ), .c11(\矩阵乘法_2_c11 ), .c12(\矩阵乘法_2_c12 ), .c21(\矩阵乘法_2_c21 ),
    .c22(\矩阵乘法_2_c22 ));
  \矩阵MUX  \u_矩阵mux_2  (
    .A11(\矩阵初始值_1_out11 ), .A12(\矩阵初始值_1_out12 ), .A21(\矩阵初始值_1_out21 ), .A22(\矩阵初始值_1_out22 ),
    .B11(\矩阵乘法_1_c11 ), .B12(\矩阵乘法_1_c12 ), .B21(\矩阵乘法_1_c21 ), .B22(\矩阵乘法_1_c22 ), .select(init),
    .out11(\矩阵mux_2_out11 ), .out12(\矩阵mux_2_out12 ), .out21(\矩阵mux_2_out21 ), .out22(\矩阵mux_2_out22 ));
  \单位阵  \u_单位阵_2  (.out11(\单位阵_2_out11 ), .out12(\单位阵_2_out12 ), .out21(\单位阵_2_out21 ), .out22(\单位阵_2_out22 ));
  \矩阵MUX  \u_矩阵mux_3  (
    .A11(\单位阵_2_out11 ), .A12(\单位阵_2_out12 ), .A21(\单位阵_2_out21 ), .A22(\单位阵_2_out22 ), .B11(\矩阵乘法_2_c11 ),
    .B12(\矩阵乘法_2_c12 ), .B21(\矩阵乘法_2_c21 ), .B22(\矩阵乘法_2_c22 ), .select(init), .out11(\矩阵mux_3_out11 ),
    .out12(\矩阵mux_3_out12 ), .out21(\矩阵mux_3_out21 ), .out22(\矩阵mux_3_out22 ));
  \矩阵寄存器  \u_矩阵寄存器_1  (
    .A11_in(\矩阵mux_2_out11 ), .A12_in(\矩阵mux_2_out12 ), .A21_in(\矩阵mux_2_out21 ), .A22_in(\矩阵mux_2_out22 ),
    .enable(ena), .clock(clk), .clear(clr), .A11_out(a11), .A12_out(a12), .A21_out(a21), .A22_out(a22));
  \矩阵寄存器  \u_矩阵寄存器_2  (
    .A11_in(\矩阵mux_3_out11 ), .A12_in(\矩阵mux_3_out12 ), .A21_in(\矩阵mux_3_out21 ), .A22_in(\矩阵mux_3_out22 ),
    .enable(ena), .clock(clk), .clear(clr), .A11_out(s11), .A12_out(s12), .A21_out(s21), .A22_out(s22));
  Multiplexer #(.width(32)) multiplexer_1 (.in0({32{1'b0}}), .in1(s12), .out(out_4), .sel(freeze));  // open: en
endmodule

module \计数逻辑  (
  input  [31:0] \input ,
  input  in_2,
  output n_low,
  output freeze
);

  wire clk, comparator_1_eq, init;
  wire [31:0] multiplexer_1_out, n, shifter_1_out;

  Counter #(.width(1), .max('h1), .ongoal("stay")) counter_1 (
    .Q(init), .clk(clk), .clr(in_2));  // open: load, D, count, carry
  Clock clock_1 (.out(clk));
  Shifter #(.width(32), .shift("lr")) shifter_1 (.in(n), .\dist (5'b00001), .out(shifter_1_out));
  Comparator #(.width(32), .mode("unsigned")) comparator_1 (
    .a(n), .b({32{1'b0}}), .eq(comparator_1_eq));  // open: gt, lt
  Register #(.width(32)) register_1 (.D(multiplexer_1_out), .Q(n), .clk(clk), .clr(in_2));  // open: en
  Multiplexer #(.width(32)) multiplexer_1 (
    .in0(\input ), .in1(shifter_1_out), .out(multiplexer_1_out), .sel(init));  // open: en
  Bit_Extender #(.in_width(32), .out_width(1)) bit_extender_1 (.in(n), .out(n_low));
  Multiplexer multiplexer_2 (.in0(1'b0), .in1(comparator_1_eq), .out(freeze), .sel(init));  // open: en

  // Other names for the same wires on the sheet: clr = in_2
endmodule

module \单位阵  (
  output [31:0] out11,
  output [31:0] out12,
  output [31:0] out21,
  output [31:0] out22
);


  assign out11 = 32'h1;
  assign out12 = {32{1'b0}};
  assign out21 = {32{1'b0}};
  assign out22 = 32'h1;
endmodule
