// Logisim project Logisim_mod.circ as structural Verilog: 3 circuits, main circuit 状态转移
module \状态转移  (
  input  [1:0] C,
  input  B,
  output [1:0] C_
);

  wire and_1_out, and_2_out, and_3_out, and_4_out, and_5_out, and_6_out, not_1_out, not_2_out, not_3_out,
       not_4_out, not_5_out, not_6_out, not_7_out, not_8_out;

  not not_1 (not_1_out, C[0]);
  not not_2 (not_2_out, C[1]);
  not not_3 (not_3_out, C[0]);
  not not_4 (not_4_out, C[1]);
  not not_5 (not_5_out, C[0]);
  not not_6 (not_6_out, B);
  not not_7 (not_7_out, C[1]);
  not not_8 (not_8_out, B);
  and and_1 (and_1_out, not_1_out, C[1]);
  and and_2 (and_2_out, C[0], not_2_out);
  and and_3 (and_3_out, not_3_out, not_4_out, B);
  and and_4 (and_4_out, not_5_out, C[1], not_6_out);
  and and_5 (and_5_out, C[0], not_7_out, not_8_out);
  and and_6 (and_6_out, C[0], C[1], B);
  or or_1 (C_[0], and_1_out, and_2_out);
  or or_2 (C_[1], and_3_out, and_4_out, and_5_out, and_6_out);
endmodule

module \状态输出  (
  input  [1:0] in_1,
  input  B,
  output S0,
  output S1,
  output S2,
  output S3,
  output S4
);

  wire and_1_out, and_2_out, and_3_out, and_4_out, and_5_out, and_6_out, and_7_out, and_8_out, not_1_out,
       not_2_out, not_3_out, not_4_out, not_5_out, not_6_out, not_7_out, not_8_out, not_9_out, not_10_out,
       not_11_out, not_12_out;

  not not_1 (not_1_out, in_1[0]);
  not not_2 (not_2_out, in_1[1]);
  not not_3 (not_3_out, B);
  not not_4 (not_4_out, B);
  not not_5 (not_5_out, in_1[0]);
  not not_6 (not_6_out, in_1[1]);
  not not_7 (not_7_out, in_1[0]);
  not not_8 (not_8_out, in_1[1]);
  not not_9 (not_9_out, in_1[0]);
  not not_10 (not_10_out, B);
  not not_11 (not_11_out, in_1[1]);
  not not_12 (not_12_out, B);
  and and_1 (and_1_out, not_1_out, not_2_out, not_3_out);
  and and_2 (and_2_out, in_1[0], in_1[1], not_4_out);
  and and_3 (and_3_out, not_5_out, not_6_out, B);
  and and_4 (and_4_out, in_1[0], in_1[1], B);
  and and_5 (and_5_out, not_7_out, in_1[1], B);
  and and_6 (and_6_out, in_1[0], not_8_out, B);
  and and_7 (and_7_out, not_9_out, in_1[1], not_10_out);
  and and_8 (and_8_out, in_1[0], not_11_out, not_12_out);
  or or_1 (S1, and_1_out, and_2_out);
  or or_2 (S2, and_3_out, and_4_out);
  or or_3 (S3, and_5_out, and_6_out);
  or or_4 (S4, and_7_out, and_8_out);

  assign S0 = 1'b0;
endmodule

module mod5 (
  input  in_1,
  output out_2,
  output out_3,
  output out_4,
  output out_5,
  output out_6
);

  wire clock_1_out;
  wire [1:0] register_1_q, \状态转移_1_c_ ;

  \状态转移  \u_状态转移_1  (.B(in_1), .C(register_1_q), .C_(\状态转移_1_c_ ));
  Register #(.width(2)) register_1 (.D(\状态转移_1_c_ ), .Q(register_1_q), .clk(clock_1_out));  // open: en, clr
  Clock clock_1 (.out(clock_1_out));
  \状态输出  \u_状态输出_1  (.B(in_1), .in_1(register_1_q), .S0(out_2), .S1(out_3), .S2(out_4), .S3(out_5), .S4(out_6));
endmodule
