// Logisim project Logisim_swap.circ as structural Verilog: 4 circuits, main circuit 1bit_swap
module _1bit_swap (
  input  I1,
  input  I2,
  input  S,
  output x,
  output y
);

  wire and_1_out, and_2_out, and_3_out, and_4_out, not_1_out, not_2_out;

  not not_1 (not_1_out, S);
  not not_2 (not_2_out, S);
  and and_1 (and_1_out, I1, not_1_out);
  and and_2 (and_2_out, I2, S);
  and and_3 (and_3_out, I2, not_2_out);
  and and_4 (and_4_out, I1, S);
  or or_1 (x, and_1_out, and_2_out);
  or or_2 (y, and_3_out, and_4_out);
endmodule

module _4bit_swap (
  input  [3:0] I1,
  input  [3:0] I2,
  input  enable,
  output [3:0] _01,
  output [3:0] _02
);

  _1bit_swap u_1bit_swap_1 (.I1(I1[0]), .I2(I2[0]), .S(enable), .x(_01[0]), .y(_02[0]));
  _1bit_swap u_1bit_swap_2 (.I1(I1[1]), .I2(I2[1]), .S(enable), .x(_01[1]), .y(_02[1]));
  _1bit_swap u_1bit_swap_3 (.I1(I1[2]), .I2(I2[2]), .S(enable), .x(_01[2]), .y(_02[2]));
  _1bit_swap u_1bit_swap_4 (.I1(I1[3]), .I2(I2[3]), .S(enable), .x(_01[3]), .y(_02[3]));

  // Other names for the same wires on the sheet: _01_0 = _01[0]; _01_1 = _01[1]; _01_2 = _01[2]; _01_3 = _01[3];
  //   _02_0 = _02[0]; _02_1 = _02[1]; _02_2 = _02[2]; _02_3 = _02[3]; I1_0 = I1[0]; I1_1 = I1[1]; I1_2 = I1[2];
  //   I1_3 = I1[3]; I2_0 = I2[0]; I2_1 = I2[1]; I2_2 = I2[2]; I2_3 = I2[3]
endmodule

module l_swap (
  input  [3:0] I1,
  input  [3:0] I2,
  output [3:0] O1,
  output [3:0] O2
);

  wire comparator_1_gt;

  Comparator #(.width(4), .mode("unsigned")) comparator_1 (.a(I1), .b(I2), .gt(comparator_1_gt));  // open: eq, lt
  _4bit_swap u_4bit_swap_1 (.I1(I1), .I2(I2), .enable(comparator_1_gt), ._01(O1), ._02(O2));
endmodule

module _4bit_sort (
  input  [3:0] A,
  input  [3:0] B,
  input  [3:0] C,
  input  [3:0] D,
  output [3:0] O1,
  output [3:0] O2,
  output [3:0] O3,
  output [3:0] O4
);

  wire [3:0] l_swap_1_o1, l_swap_1_o2, l_swap_2_o1, l_swap_2_o2, l_swap_3_o1, l_swap_4_o1, l_swap_4_o2,
       l_swap_6_o1;

  l_swap l_swap_1 (.I1(A), .I2(B), .O1(l_swap_1_o1), .O2(l_swap_1_o2));
  l_swap l_swap_2 (.I1(l_swap_1_o2), .I2(C), .O1(l_swap_2_o1), .O2(l_swap_2_o2));
  l_swap l_swap_3 (.I1(l_swap_2_o2), .I2(D), .O1(l_swap_3_o1), .O2(O4));
  l_swap l_swap_4 (.I1(l_swap_1_o1), .I2(l_swap_2_o1), .O1(l_swap_4_o1), .O2(l_swap_4_o2));
  l_swap l_swap_5 (.I1(l_swap_4_o1), .I2(l_swap_6_o1), .O1(O1), .O2(O2));
  l_swap l_swap_6 (.I1(l_swap_4_o2), .I2(l_swap_3_o1), .O1(l_swap_6_o1), .O2(O3));
endmodule
