// Logisim project ftoi.circ as structural Verilog: 2 circuits, main circuit ftoi
module ftoi (
  input  [15:0] float,
  output [31:0] \int 
);

  wire and_1_out, comparator_1_lt, comparator_2_eq, not_2_out, not_3_out;
  wire [31:0] adder_1_out, calculate_1_out_3, multiplexer_1_out, not_1_out;

  calculate calculate_1 (.In1(float[9:0]), .In2(float[14:10]), .out_3(calculate_1_out_3));
  Comparator #(.width(5), .mode("unsigned")) comparator_1 (
    .a(float[14:10]), .b(5'b01111), .lt(comparator_1_lt));  // open: gt, eq
  Comparator #(.width(5), .mode("unsigned")) comparator_2 (
    .a(float[14:10]), .b({5{1'b1}}), .eq(comparator_2_eq));  // open: gt, lt
  assign not_1_out = ~calculate_1_out_3;  // NOT_Gate not_1, 32 bits wide
  not not_2 (not_2_out, comparator_1_lt);
  not not_3 (not_3_out, comparator_2_eq);
  Adder #(.width(32)) adder_1 (.a(not_1_out), .b(32'h1), .out(adder_1_out));  // open: cin, cout
  Multiplexer #(.width(32)) multiplexer_1 (
    .in0(calculate_1_out_3), .in1(adder_1_out), .out(multiplexer_1_out), .sel(float[15]));  // open: en
  and and_1 (and_1_out, not_2_out, not_3_out);
  Multiplexer #(.width(32)) multiplexer_2 (
    .in0({32{1'b0}}), .in1(multiplexer_1_out), .out(\int ), .sel(and_1_out));  // open: en
endmodule

module calculate (
  input  [9:0] In1,
  input  [4:0] In2,
  output [31:0] out_3
);

  wire comparator_1_eq;
  wire [4:0] subtractor_1_out;
  wire [10:0] bit_extender_1_out, multiplexer_1_out;
  wire [31:0] bit_extender_2_out, shifter_1_out;

  assign bit_extender_1_out = {{1{1'b0}}, In1};  // Bit_Extender bit_extender_1
  Comparator #(.width(5), .mode("unsigned")) comparator_1 (
    .a({5{1'b0}}), .b(In2), .eq(comparator_1_eq));  // open: gt, lt
  assign bit_extender_2_out = {{21{1'b0}}, multiplexer_1_out};  // Bit_Extender bit_extender_2
  Multiplexer #(.width(11)) multiplexer_1 (
    .in0({1'b1, In1}), .in1(bit_extender_1_out), .out(multiplexer_1_out), .sel(comparator_1_eq));  // open: en
  Subtractor #(.width(5)) subtractor_1 (.a(In2), .b(5'b01111), .out(subtractor_1_out));  // open: bin, bout
  Shifter #(.width(32)) shifter_1 (.in(bit_extender_2_out), .\dist (subtractor_1_out), .out(shifter_1_out));
  Shifter #(.width(32), .shift("lr")) shifter_2 (.in(shifter_1_out), .\dist (5'b01010), .out(out_3));
endmodule
