// Logisim project 三进制半加器.circ as structural Verilog: 1 circuit, main circuit main
module main (
  input  [1:0] in_1,
  input  [1:0] in_2,
  output [1:0] out_3,
  output o3
);

  wire and_1_out, and_2_out, and_3_out, and_4_out, and_5_out, and_6_out, and_7_out, and_8_out, and_9_out,
       not_1_out, not_2_out, not_3_out, not_4_out, not_5_out, not_6_out, not_7_out, not_8_out;

  not not_1 (not_1_out, in_1[1]);
  and and_1 (and_1_out, not_1_out, not_2_out, in_2[1]);
  not not_2 (not_2_out, in_1[0]);
  and and_2 (and_2_out, in_1[0], in_2[0]);
  not not_3 (not_3_out, in_2[1]);
  and and_3 (and_3_out, in_1[1], not_3_out, not_4_out);
  not not_4 (not_4_out, in_2[0]);
  not not_5 (not_5_out, in_1[1]);
  not not_6 (not_6_out, in_1[0]);
  and and_4 (and_4_out, not_5_out, not_6_out, in_2[0]);
  not not_7 (not_7_out, in_2[1]);
  and and_5 (and_5_out, in_1[0], not_7_out, not_8_out);
  not not_8 (not_8_out, in_2[0]);
  and and_6 (and_6_out, in_1[1], in_2[1]);
  and and_7 (and_7_out, in_1[0], in_2[1]);
  and and_8 (and_8_out, in_1[1], in_2[0]);
  and and_9 (and_9_out, in_1[1], in_2[1]);
  or or_1 (out_3[1], and_1_out, and_2_out, and_3_out);
  or or_2 (out_3[0], and_4_out, and_5_out, and_6_out);
  or or_3 (o3, and_7_out, and_8_out, and_9_out);
endmodule
