// Logisim project 售货机.circ as structural Verilog: 2 circuits, main circuit main
module main (
  input  in,
  input  clr,
  output changes,
  output goods
);

  wire clk_out, comparator_1_eq;
  wire [2:0] register_1_q, \状态转移_1_out_3 ;

  Clock clk (.out(clk_out));
  \状态转移  \u_状态转移_1  (.in(in), .in_2(register_1_q), .out_3(\状态转移_1_out_3 ));
  Register #(.width(3)) register_1 (.D(\状态转移_1_out_3 ), .Q(register_1_q), .clk(clk_out), .clr(clr));  // open: en
  Comparator #(.width(1), .mode("unsigned")) comparator_1 (
    .a(1'b1), .b(register_1_q[0]), .eq(comparator_1_eq));  // open: gt, lt
  Comparator #(.width(1), .mode("unsigned")) comparator_2 (.a(register_1_q[2]), .b(1'b1), .eq(goods));  // open: gt, lt
  and and_1 (changes, comparator_1_eq, goods);
endmodule

module \状态转移  (
  input  in,
  input  [2:0] in_2,
  output [2:0] out_3
);

  wire and_1_out, and_2_out, and_3_out, and_4_out, and_5_out, and_6_out, and_7_out, and_8_out, not_1_out,
       not_2_out, not_3_out, not_4_out, not_5_out, not_6_out, not_7_out, not_8_out, not_9_out;

  and and_1 (and_1_out, in_2[1], in_2[0]);
  and and_2 (and_2_out, in, in_2[1]);
  not not_1 (not_1_out, in_2[2]);
  and and_3 (and_3_out, not_1_out, not_2_out, in_2[0]);
  not not_2 (not_2_out, in_2[1]);
  not not_3 (not_3_out, in);
  and and_4 (and_4_out, not_3_out, in_2[1], not_4_out);
  not not_4 (not_4_out, in_2[0]);
  and and_5 (and_5_out, in, not_5_out);
  not not_5 (not_5_out, in_2[1]);
  not not_6 (not_6_out, in);
  and and_6 (and_6_out, not_6_out, not_7_out);
  not not_7 (not_7_out, in_2[0]);
  not not_8 (not_8_out, in);
  and and_7 (and_7_out, not_8_out, in_2[2]);
  and and_8 (and_8_out, in, not_9_out, in_2[0]);
  not not_9 (not_9_out, in_2[2]);
  or or_1 (out_3[2], and_1_out, and_2_out);
  or or_2 (out_3[1], and_3_out, and_4_out, and_5_out);
  or or_3 (out_3[0], and_6_out, and_7_out, and_8_out);
endmodule
