// Logisim project 抢答器.circ as structural Verilog: 1 circuit, main circuit main
module main (
  input  I1,
  input  I2,
  input  I3,
  input  I4,
  input  reset
);

  wire clock_1_out, d_ff_1_q, d_ff_1_qn, d_ff_2_q, d_ff_2_qn, d_ff_3_q, d_ff_3_qn, d_ff_4_q, d_ff_4_qn,
       nand_1_out;

  Clock clock_1 (.out(clock_1_out));
  D_Flip_Flop d_ff_1 (.clk(nand_1_out), .D(I1), .Q(d_ff_1_q), .Qn(d_ff_1_qn), .reset(reset));  // open: preset, en
  D_Flip_Flop d_ff_2 (.clk(nand_1_out), .D(I2), .Q(d_ff_2_q), .Qn(d_ff_2_qn), .reset(reset));  // open: preset, en
  D_Flip_Flop d_ff_3 (.clk(nand_1_out), .D(I3), .Q(d_ff_3_q), .Qn(d_ff_3_qn), .reset(reset));  // open: preset, en
  D_Flip_Flop d_ff_4 (.clk(nand_1_out), .D(I4), .Q(d_ff_4_q), .Qn(d_ff_4_qn), .reset(reset));  // open: preset, en
  LED led_1 (.in(d_ff_1_q));
  LED led_2 (.in(d_ff_2_q));
  nand nand_1 (nand_1_out, d_ff_1_qn, d_ff_2_qn, d_ff_3_qn, d_ff_4_qn, clock_1_out);
  LED led_3 (.in(d_ff_3_q));
  LED led_4 (.in(d_ff_4_q));
endmodule
